// Logisim project Single-Cycle_Processor.circ as structural Verilog: 15 circuits, main circuit main
module main (
  input  [1:0] in_1,
  input  CLR
);

  wire CLK_out, control_unit_1_alusrc, control_unit_1_bl, control_unit_1_bx, control_unit_1_memtoreg,
       control_unit_1_memwrite, control_unit_1_mov, control_unit_1_pcsrc, control_unit_1_regwrite,
       logisim_led_1_out_2;
  wire [1:0] control_unit_1_alucontrol_1_0, control_unit_1_immsrc_1_0, control_unit_1_regsrc_1_0,
       mega_splitter_1_op;
  wire [3:0] alu_1_flags, mega_splitter_1_cond, mega_splitter_1_rd, mega_splitter_1_rd_2, mega_splitter_1_rm,
       mega_splitter_1_rn, multiplexer_2_out, multiplexer_3_out, multiplexer_4_out, multiplexer_5_out;
  wire [5:0] mega_splitter_1_funct;
  wire [23:0] mega_splitter_1__27_4, mega_splitter_1_extend;
  wire [31:0] adder_1_out, adder_2_out, alu_1_result, data_memory_1_rd, extender_1_extimm,
       instruction_memory_1_rd, multiplexer_1_out, multiplexer_6_out, multiplexer_7_out, multiplexer_8_out,
       multiplexer_9_out, multiplexer_10_out, r0, r1, r2, r3, r4, r5, r6, r7, r8, r9, r10, r11, r12, r13,
       r14, r15, register_file_1_rd1, register_file_1_rd2;

  Clock CLK (.out(CLK_out));
  // Probe on adder_1_out
  // Probe on r0
  Multiplexer #(.width(32), .enable("false")) multiplexer_1 (
    .in0(adder_1_out), .in1(multiplexer_9_out), .out(multiplexer_1_out), .sel(control_unit_1_pcsrc));
  // Probe on multiplexer_1_out
  // Probe on multiplexer_9_out
  LED Done (.in(logisim_led_1_out_2));
  Register #(.width(32)) PC (.D(multiplexer_1_out), .Q(r15), .clk(CLK_out), .clr(CLR));  // open: en
  // Probe on r15
  // Probe on r1
  // Probe on instruction_memory_1_rd
  Logisim_LED logisim_led_1 (.in_1(instruction_memory_1_rd), .out_2(logisim_led_1_out_2));
  // Probe on r2
  // Probe on mega_splitter_1_cond
  // Probe on mega_splitter_1_op
  // Probe on mega_splitter_1_funct
  Instruction_Memory instruction_memory_1 (.in_2(r15), .rd(instruction_memory_1_rd), .in_1(in_1));
  Adder #(.width(32)) adder_1 (.a(r15), .b(32'h4), .out(adder_1_out));  // open: cin, cout
  // Probe on adder_1_out
  // Probe on mega_splitter_1_rd
  Mega_Splitter mega_splitter_1 (
    .in_1(instruction_memory_1_rd), .cond(mega_splitter_1_cond), .op(mega_splitter_1_op),
    .funct(mega_splitter_1_funct), .rd(mega_splitter_1_rd), .rn(mega_splitter_1_rn), .rm(mega_splitter_1_rm),
    .rd_2(mega_splitter_1_rd_2), .extend(mega_splitter_1_extend), ._27_4(mega_splitter_1__27_4));
  // Probe on mega_splitter_1_rm
  // Probe on r3
  // Probe on mega_splitter_1_rd_2
  // Probe on mega_splitter_1_rn
  Adder #(.width(32)) adder_2 (.a(adder_1_out), .b(32'h4), .out(adder_2_out));  // open: cin, cout
  Multiplexer #(.width(4), .enable("false")) multiplexer_2 (
    .in0(mega_splitter_1_rn), .in1(4'b1111), .out(multiplexer_2_out), .sel(control_unit_1_regsrc_1_0[0]));
  // Probe on adder_2_out
  // Probe on r4
  Multiplexer #(.width(4), .enable("false")) multiplexer_3 (
    .in0(mega_splitter_1_rm), .in1(mega_splitter_1_rd_2), .out(multiplexer_3_out),
    .sel(control_unit_1_regsrc_1_0[1]));
  // Probe on r5
  Control_Unit control_unit_1 (
    .cond(mega_splitter_1_cond), .op(mega_splitter_1_op), .funct(mega_splitter_1_funct),
    .rd(mega_splitter_1_rd), .alu_flags(alu_1_flags), .PCSrc(control_unit_1_pcsrc),
    .MemtoReg(control_unit_1_memtoreg), .MemWrite(control_unit_1_memwrite),
    .ALUControl_1_0(control_unit_1_alucontrol_1_0), .ALUSrc(control_unit_1_alusrc),
    .ImmSrc_1_0(control_unit_1_immsrc_1_0), .RegWrite(control_unit_1_regwrite),
    .RegSrc_1_0(control_unit_1_regsrc_1_0), .CLK(CLK_out), .Funct_27_4(mega_splitter_1__27_4), .CLR(CLR),
    .Mov(control_unit_1_mov), .BX(control_unit_1_bx), .BL(control_unit_1_bl));
  Multiplexer #(.width(4), .enable("false")) multiplexer_4 (
    .in0(multiplexer_2_out), .in1(mega_splitter_1_rm), .out(multiplexer_4_out), .sel(control_unit_1_bx));
  Multiplexer #(.width(4), .enable("false")) multiplexer_5 (
    .in0(mega_splitter_1_rd_2), .in1(4'b1110), .out(multiplexer_5_out), .sel(control_unit_1_bl));
  Multiplexer #(.width(32), .enable("false")) multiplexer_6 (
    .in0(multiplexer_10_out), .in1(adder_1_out), .out(multiplexer_6_out), .sel(control_unit_1_bl));
  // Probe on r6
  // Probe on r7
  Extender extender_1 (._0_23(mega_splitter_1_extend), .ExtImm(extender_1_extimm), .ImmSrc(control_unit_1_immsrc_1_0));
  // Probe on r8
  Register_File register_file_1 (
    .a1(multiplexer_4_out), .a2(multiplexer_3_out), .a3(multiplexer_5_out), .wd3(multiplexer_6_out),
    .r15__PC_8(adder_2_out), .rd1(register_file_1_rd1), .rd2(register_file_1_rd2), .CLK(CLK_out),
    .we3(control_unit_1_regwrite), .CLR(CLR), .r14(r14), .r13(r13), .r12(r12), .r11(r11), .r10(r10), .r9(r9),
    .r8(r8), .r7(r7), .r6(r6), .r5(r5), .r4(r4), .r3(r3), .r2(r2), .r1(r1), .r0(r0));
  // Probe on r9
  // Probe on r10
  Multiplexer #(.width(32), .enable("false")) multiplexer_7 (
    .in0(register_file_1_rd1), .in1({32{1'b0}}), .out(multiplexer_7_out), .sel(control_unit_1_mov));
  Multiplexer #(.width(32), .enable("false")) multiplexer_8 (
    .in0(register_file_1_rd2), .in1(extender_1_extimm), .out(multiplexer_8_out), .sel(control_unit_1_alusrc));
  Multiplexer #(.width(32), .enable("false")) multiplexer_9 (
    .in0(multiplexer_10_out), .in1(multiplexer_7_out), .out(multiplexer_9_out), .sel(control_unit_1_bx));
  // Probe on r11
  // Probe on alu_1_flags
  ALU alu_1 (
    .a(multiplexer_7_out), .b(multiplexer_8_out), .result(alu_1_result), .flags(alu_1_flags),
    .in_1(control_unit_1_alucontrol_1_0));
  // Probe on r12
  // Probe on r13
  Data_Memory data_memory_1 (
    .CLK(CLK_out), .A(alu_1_result), .WD(register_file_1_rd2), .WE(control_unit_1_memwrite), .CLR(CLR),
    .RD(data_memory_1_rd));
  // Probe on r14
  // Probe on r15
  Multiplexer #(.width(32), .enable("false")) multiplexer_10 (
    .in0(alu_1_result), .in1(data_memory_1_rd), .out(multiplexer_10_out), .sel(control_unit_1_memtoreg));

  // Notes on the sheet:
  //   ALU Result
  //   Write Data
  //   Read Data
  //   Result
endmodule

module ALU (
  input  [1:0] in_1,
  input  [31:0] a,
  input  [31:0] b,
  output [31:0] result,
  output [3:0] flags
);

  wire adder_1_cout, not_1_out, or_2_out, subtractor_1_bout, xnor_1_out, xor_1_out;
  wire [31:0] adder_1_out, and_1_out, or_1_out, subtractor_1_out;

  assign and_1_out = a & b;  // AND_Gate and_1, 32 bits wide
  assign or_1_out = a | b;  // OR_Gate or_1, 32 bits wide
  Adder #(.width(32)) adder_1 (.a(a), .b(b), .out(adder_1_out), .cout(adder_1_cout));  // open: cin
  Subtractor #(.width(32)) subtractor_1 (.a(a), .b(b), .out(subtractor_1_out), .bout(subtractor_1_bout));  // open: bin
  Multiplexer #(.select(2), .width(32)) multiplexer_1 (
    .in0(adder_1_out), .in1(subtractor_1_out), .in2(and_1_out), .in3(or_1_out),
    .out({flags[3], result[30:0]}), .sel(in_1));  // open: en
  or or_2 (or_2_out, adder_1_cout, subtractor_1_bout);
  xor xor_1 (xor_1_out, adder_1_out[31], a[31]);
  NotExactlyOne xnor_1 (.out(xnor_1_out), .in0(in_1[0]), .in1(a[31]), .in2(b[31]));
  not not_1 (not_1_out, in_1[1]);
  Comparator #(.width(32)) comparator_1 (.a({flags[3], result[30:0]}), .b({32{1'b0}}), .eq(flags[2]));  // open: gt, lt
  and and_2 (flags[1], or_2_out, not_1_out);
  and and_3 (flags[0], not_1_out, xor_1_out, xnor_1_out);

  assign result[31] = flags[3];

  // Other names for the same wires on the sheet: control_0 = in_1[0]; control_1 = in_1[1]
endmodule

module Register_File (
  input  [3:0] a1,
  input  [3:0] a2,
  input  [31:0] wd3,
  input  CLK,
  input  CLR,
  input  we3,
  input  [3:0] a3,
  input  [31:0] r15__PC_8,
  output [31:0] rd1,
  output [31:0] rd2,
  output [31:0] r0,
  output [31:0] r1,
  output [31:0] r2,
  output [31:0] r3,
  output [31:0] r4,
  output [31:0] r5,
  output [31:0] r6,
  output [31:0] r7,
  output [31:0] r8,
  output [31:0] r9,
  output [31:0] r10,
  output [31:0] r11,
  output [31:0] r12,
  output [31:0] r13,
  output [31:0] r14
);

  wire decoder_1_out0, decoder_1_out1, decoder_1_out2, decoder_1_out3, decoder_1_out4, decoder_1_out5,
       decoder_1_out6, decoder_1_out7, decoder_1_out8, decoder_1_out9, decoder_1_out10, decoder_1_out11,
       decoder_1_out12, decoder_1_out13, decoder_1_out14;

  Decoder_part #(.select(4), .disabled(0)) decoder_1 (
    .out0(decoder_1_out0), .out1(decoder_1_out1), .out2(decoder_1_out2), .out3(decoder_1_out3),
    .out4(decoder_1_out4), .out5(decoder_1_out5), .out6(decoder_1_out6), .out7(decoder_1_out7),
    .out8(decoder_1_out8), .out9(decoder_1_out9), .out10(decoder_1_out10), .out11(decoder_1_out11),
    .out12(decoder_1_out12), .out13(decoder_1_out13), .out14(decoder_1_out14), .sel(a3), .en(we3));  // open: out15
  Register #(.width(32)) u_r0 (.D(wd3), .en(decoder_1_out0), .Q(r0), .clk(CLK), .clr(CLR));
  Register #(.width(32)) u_r1 (.D(wd3), .en(decoder_1_out1), .Q(r1), .clk(CLK), .clr(CLR));
  Register #(.width(32)) u_r2 (.D(wd3), .en(decoder_1_out2), .Q(r2), .clk(CLK), .clr(CLR));
  Register #(.width(32)) u_r3 (.D(wd3), .en(decoder_1_out3), .Q(r3), .clk(CLK), .clr(CLR));
  Register #(.width(32)) u_r4 (.D(wd3), .en(decoder_1_out4), .Q(r4), .clk(CLK), .clr(CLR));
  Register #(.width(32)) u_r5 (.D(wd3), .en(decoder_1_out5), .Q(r5), .clk(CLK), .clr(CLR));
  Register #(.width(32)) u_r6 (.D(wd3), .en(decoder_1_out6), .Q(r6), .clk(CLK), .clr(CLR));
  Register #(.width(32)) u_r7 (.D(wd3), .en(decoder_1_out7), .Q(r7), .clk(CLK), .clr(CLR));
  Register #(.width(32)) u_r8 (.D(wd3), .en(decoder_1_out8), .Q(r8), .clk(CLK), .clr(CLR));
  Register #(.width(32)) u_r9 (.D(wd3), .en(decoder_1_out9), .Q(r9), .clk(CLK), .clr(CLR));
  Register #(.width(32)) u_r10 (.D(wd3), .en(decoder_1_out10), .Q(r10), .clk(CLK), .clr(CLR));
  Register #(.width(32)) u_r11 (.D(wd3), .en(decoder_1_out11), .Q(r11), .clk(CLK), .clr(CLR));
  Register #(.width(32)) u_r12 (.D(wd3), .en(decoder_1_out12), .Q(r12), .clk(CLK), .clr(CLR));
  Register #(.width(32)) u_r13 (.D(wd3), .en(decoder_1_out13), .Q(r13), .clk(CLK), .clr(CLR));
  Register #(.width(32)) u_r14 (.D(wd3), .en(decoder_1_out14), .Q(r14), .clk(CLK), .clr(CLR));
  Multiplexer #(.select(4), .width(32)) multiplexer_1 (
    .in0(r0), .in1(r1), .in2(r2), .in3(r3), .in4(r4), .in5(r5), .in6(r6), .in7(r7), .in8(r8), .in9(r9),
    .in10(r10), .in11(r11), .in12(r12), .in13(r13), .in14(r14), .in15(r15__PC_8), .out(rd1), .sel(a1));  // open: en
  Multiplexer #(.select(4), .width(32)) multiplexer_2 (
    .in0(r0), .in1(r1), .in2(r2), .in3(r3), .in4(r4), .in5(r5), .in6(r6), .in7(r7), .in8(r8), .in9(r9),
    .in10(r10), .in11(r11), .in12(r12), .in13(r13), .in14(r14), .in15(r15__PC_8), .out(rd2), .sel(a2));  // open: en
endmodule

module Instruction_Memory (
  input  [1:0] in_1,
  input  [31:0] in_2,
  output [31:0] rd
);

  wire [31:0] rom_1_data, rom_2_data, rom_3_data, rom_4_data;

  // Probe on in_2
  ROM #(.dataWidth(32)) rom_1 (.addr(in_2[9:2]), .data(rom_1_data), .sel(1'b1));
  ROM #(.dataWidth(32)) rom_2 (.addr(in_2[9:2]), .data(rom_2_data), .sel(1'b1));
  ROM #(.dataWidth(32)) rom_3 (.addr(in_2[9:2]), .data(rom_3_data), .sel(1'b1));
  ROM #(.dataWidth(32)) rom_4 (.addr(in_2[9:2]), .data(rom_4_data), .sel(1'b1));
  Multiplexer #(.select(2), .width(32), .enable("false")) multiplexer_1 (
    .in0(rom_1_data), .in1(rom_2_data), .in2(rom_3_data), .in3(rom_4_data), .out(rd), .sel(in_1));
  // Probe on rd

  // Notes on the sheet:
  //   Sum Array
  //   Find Max
  //   Fib Iter
  //   Fib Recur
  //   contents of rom_1 (hex, n*v repeats v):
  //   e3a0dc01 e24dd004 e3a00001 e58d0000 e24dd004 e3a00002 e58d0000 e24dd004 e3a00003 e58d0000 e24dd004
  //   e3a00004 e58d0000 e24dd004 e3a00005 e58d0000 e1a0000d e3a01005 eb000000 eafffffe e3a02000 e3a03000
  //   e1520001 a000004 e5904000 e0833004 e2822001 e2800004 eafffff8 e1a00003 e12fff1e
  //   contents of rom_2 (hex, n*v repeats v):
  //   e3a0dc01 e24dd004 e3a00001 e58d0000 e24dd004 e3a00002 e58d0000 e24dd004 e3a00003 e58d0000 e24dd004
  //   e3a00004 e58d0000 e24dd004 e3a00005 e58d0000 e1a0000d e3a01005 eb000000 eafffffe e24dd004 e58d4000
  //   e3a02000 e5903000 e1520001 a000005 e5904000 e1530004 b1a03004 e2800004 e2822001 eafffff7 e59d4000
  //   e28dd004 e1a00003 e12fff1e
  //   contents of rom_3 (hex, n*v repeats v):
  //   e3a0dc01 e3a0000b eb000000 eafffffe e24dd004 e58d4000 e3a01000 e3a02001 e3a03002 e3500002 ba000006
  //   e1530000 ca000009 e0814002 e1a01002 e1a02004 e2833001 eafffff8 e3500000 3a00000 e3500001 3a00001
  //   e12fff1e e1a00004 e59d4000 e28dd004 e12fff1e
  //   contents of rom_4 (hex, n*v repeats v):
  //   e3a0dc01 e3a0000a eb000000 eafffffe e24dd010 e58de000 e3500000 a000012 e3500001 a000010 e28dd004
  //   e58d0000 e24dd004 e2400001 ebfffff4 e28dd008 e58d0000 e24dd008 e28dd004 e59d0000 e24dd004 e2400002
  //   ebffffec e28dd008 e59d1000 e24dd008 e0800001 e59de000 e28dd010 e12fff1e
endmodule

// Data Memory
module Data_Memory (
  input  CLK,
  input  [31:0] A,
  input  [31:0] WD,
  input  WE,
  input  CLR,
  output [31:0] RD
);

  wire not_1_out;

  not not_1 (not_1_out, WE);
  RAM #(.dataWidth(32), .bus("separate")) ram_1 (
    .addr(A[9:2]), .din(WD), .data(RD), .str(WE), .sel(1'b1), .clk(CLK), .ld(not_1_out), .clr(CLR));
  // Probe on RD
endmodule

module Mega_Splitter (
  input  [31:0] in_1,
  output [23:0] _27_4,
  output [3:0] cond,
  output [1:0] op,
  output [5:0] funct,
  output [3:0] rd,
  output [3:0] rn,
  output [3:0] rm,
  output [3:0] rd_2,
  output [23:0] extend
);


  assign _27_4 = in_1[27:4];
  assign cond = in_1[31:28];
  assign extend = in_1[23:0];
  assign funct = in_1[25:20];
  assign op = in_1[27:26];
  assign rd = in_1[15:12];
  assign rd_2 = in_1[15:12];
  assign rm = in_1[3:0];
  assign rn = in_1[19:16];
endmodule

// Control Unit
module Control_Unit (
  input  CLK,
  input  [3:0] cond,
  input  [3:0] alu_flags,
  input  [3:0] rd,
  input  [5:0] funct,
  input  [1:0] op,
  input  [23:0] Funct_27_4,
  input  CLR,
  output PCSrc,
  output RegWrite,
  output MemWrite,
  output Mov,
  output BX,
  output MemtoReg,
  output ALUSrc,
  output [1:0] ImmSrc_1_0,
  output [1:0] RegSrc_1_0,
  output [1:0] ALUControl_1_0,
  output BL
);

  wire decoder_1_bx, decoder_1_memw, decoder_1_mov, decoder_1_nowrite, decoder_1_pcs, decoder_1_regw;
  wire [1:0] decoder_1_flagw_1_0;

  Decoder decoder_1 (
    .Rd_3_0(rd), .Funct_5_0(funct), .Op_1_0(op), .Funct_27_4(Funct_27_4), .PCS(decoder_1_pcs),
    .RegW(decoder_1_regw), .MemW(decoder_1_memw), .MemtoReg(MemtoReg), .ALUSrc(ALUSrc),
    .ImmSrc_1_0(ImmSrc_1_0), .RegSrc_1_0(RegSrc_1_0), .BL(BL), .BX(decoder_1_bx),
    .NoWrite(decoder_1_nowrite), .ALUControl_1_0(ALUControl_1_0), .FlagW_1_0(decoder_1_flagw_1_0),
    .Mov(decoder_1_mov));
  Conditional_Logic conditional_logic_1 (
    .PCS(decoder_1_pcs), .RegW(decoder_1_regw), .NoWrite(decoder_1_nowrite), .MemW(decoder_1_memw),
    .FlagW(decoder_1_flagw_1_0), .Cond(cond), .CLK(CLK), .CLR(CLR), .ALUFlags(alu_flags), .PCSrc(PCSrc),
    .RegWrite(RegWrite), .MemWrite(MemWrite), .Mov(decoder_1_mov), .BX(decoder_1_bx), .Mov_2(Mov), .BX_2(BX));
endmodule

module Decoder (
  input  [3:0] Rd_3_0,
  input  [5:0] Funct_5_0,
  input  [1:0] Op_1_0,
  input  [23:0] Funct_27_4,
  output PCS,
  output RegW,
  output MemW,
  output MemtoReg,
  output ALUSrc,
  output [1:0] ImmSrc_1_0,
  output [1:0] RegSrc_1_0,
  output BL,
  output BX,
  output NoWrite,
  output [1:0] ALUControl_1_0,
  output [1:0] FlagW_1_0,
  output Mov
);

  wire main_decoder_1_aluop, main_decoder_1_branch;

  PC_Logic pc_logic_1 (.Rd(Rd_3_0), .B(main_decoder_1_branch), .RegW(RegW), .PCS(PCS));
  Main_Decoder main_decoder_1 (
    .Funct_27_4(Funct_27_4), .Branch(main_decoder_1_branch), .MemtoReg(MemtoReg), .MemW(MemW),
    .ALUSrc(ALUSrc), .ImmSrc(ImmSrc_1_0), .RegW(RegW), .RegSrc(RegSrc_1_0), .ALUOp(main_decoder_1_aluop),
    .BL(BL), .BX(BX), .op0(Op_1_0[0]), .op1(Op_1_0[1]), .Funct_5_0(Funct_5_0));
  ALU_Decoder ALU_Decoder (
    .ALUControl(ALUControl_1_0), .FlagW(FlagW_1_0), .NoWrite(NoWrite), .Mov(Mov),
    .ALUOp(main_decoder_1_aluop), .Funct_4_0(Funct_5_0[4:0]));
endmodule

// PC Logic
module PC_Logic (
  input  [3:0] Rd,
  input  B,
  input  RegW,
  output PCS
);

  wire and_1_out, comparator_1_eq;

  Comparator #(.width(4)) comparator_1 (.a(Rd), .b(4'b1111), .eq(comparator_1_eq));  // open: gt, lt
  and and_1 (and_1_out, comparator_1_eq, RegW);
  or or_1 (PCS, and_1_out, B);
endmodule

// Main Decoder
module Main_Decoder (
  input  [5:0] Funct_5_0,
  input  [23:0] Funct_27_4,
  input  op0,
  input  op1,
  output Branch,
  output MemtoReg,
  output MemW,
  output ALUSrc,
  output [1:0] ImmSrc,
  output RegW,
  output [1:0] RegSrc,
  output ALUOp,
  output BL,
  output BX
);

  wire DP_Imm_out, DP_Reg_out;

  Comparator #(.width(24)) comparator_1 (.a(Funct_27_4), .b(24'h12fff1), .eq(BX));  // open: gt, lt
  and DP_Reg (DP_Reg_out, ~op0, ~op1, ~Funct_5_0[5], ~BX);  // AND_Gate
  and DP_Imm (DP_Imm_out, ~op0, ~op1, Funct_5_0[5], ~BX);  // AND_Gate
  and STR (MemW, op0, ~op1, ~Funct_5_0[0], ~BX);  // AND_Gate
  and LDR (MemtoReg, op0, ~op1, Funct_5_0[0], ~BX);  // AND_Gate
  and B (Branch, ~op0, op1, ~BX);  // AND_Gate
  and and_1 (BL, Funct_5_0[4], Branch);
  or or_1 (ImmSrc[0], MemW, MemtoReg);
  or or_2 (RegSrc[0], Branch, BL, BX);
  or or_3 (ALUSrc, DP_Imm_out, MemW, MemtoReg, Branch);
  or or_4 (RegW, DP_Reg_out, DP_Imm_out, MemtoReg, BL, BX);
  or or_5 (ALUOp, DP_Reg_out, DP_Imm_out);

  assign ImmSrc[1] = Branch;
  assign RegSrc[1] = MemW;

  // Notes on the sheet:
  //   Type
  //   DP Reg
  //   DP Imm
  //   STR
  //   B
  //   LDR
endmodule

module ALU_Decoder (
  input  [4:0] Funct_4_0,
  input  ALUOp,
  output [1:0] ALUControl,
  output [1:0] FlagW,
  output NoWrite,
  output Mov
);

  wire ADD_0_out, ADD_1_out, AND_0_out, AND_1_out, ORR_0_out, ORR_1_out, SUB_0_out, SUB_1_out;

  and ADD_0 (ADD_0_out, ALUOp, ~Funct_4_0[4], Funct_4_0[3], ~Funct_4_0[2], ~Funct_4_0[1], ~Funct_4_0[0]);  // AND_Gate
  and ADD_1 (ADD_1_out, ALUOp, ~Funct_4_0[4], Funct_4_0[3], ~Funct_4_0[2], ~Funct_4_0[1], Funct_4_0[0]);  // AND_Gate
  and SUB_0 (SUB_0_out, ALUOp, ~Funct_4_0[4], ~Funct_4_0[3], Funct_4_0[2], ~Funct_4_0[1], ~Funct_4_0[0]);  // AND_Gate
  and SUB_1 (SUB_1_out, ALUOp, ~Funct_4_0[4], ~Funct_4_0[3], Funct_4_0[2], ~Funct_4_0[1], Funct_4_0[0]);  // AND_Gate
  and AND_0 (AND_0_out, ALUOp, ~Funct_4_0[4], ~Funct_4_0[3], ~Funct_4_0[2], ~Funct_4_0[1], ~Funct_4_0[0]);  // AND_Gate
  and AND_1 (AND_1_out, ALUOp, ~Funct_4_0[4], ~Funct_4_0[3], ~Funct_4_0[2], ~Funct_4_0[1], Funct_4_0[0]);  // AND_Gate
  and ORR_0 (ORR_0_out, ALUOp, Funct_4_0[4], Funct_4_0[3], ~Funct_4_0[2], ~Funct_4_0[1], ~Funct_4_0[0]);  // AND_Gate
  and ORR_1 (ORR_1_out, ALUOp, Funct_4_0[4], Funct_4_0[3], ~Funct_4_0[2], ~Funct_4_0[1], Funct_4_0[0]);  // AND_Gate
  and CMP (NoWrite, ALUOp, Funct_4_0[4], ~Funct_4_0[3], Funct_4_0[2], ~Funct_4_0[1], Funct_4_0[0]);  // AND_Gate
  and u_MOV (Mov, ALUOp, Funct_4_0[4], Funct_4_0[3], ~Funct_4_0[2], Funct_4_0[1], ~Funct_4_0[0]);  // AND_Gate
  or Control_0 (ALUControl[0], SUB_0_out, SUB_1_out, ORR_0_out, ORR_1_out, NoWrite);
  or Control_1 (ALUControl[1], AND_0_out, AND_1_out, ORR_0_out, ORR_1_out);
  or Flag_0 (FlagW[0], ADD_1_out, SUB_1_out, NoWrite);
  or Flag_1 (FlagW[1], ADD_1_out, SUB_1_out, AND_1_out, ORR_1_out, NoWrite);

  // Notes on the sheet:
  //   ADD_0
  //   ADD_1
  //   SUB_0
  //   SUB_1
  //   AND_1
  //   AND_0
  //   ORR_0
  //   ORR_1
  //   CMP
endmodule

// Conditional Logic
module Conditional_Logic (
  input  PCS,
  input  RegW,
  input  NoWrite,
  input  MemW,
  input  Mov,
  input  BX,
  input  [1:0] FlagW,
  input  [3:0] Cond,
  input  CLK,
  input  CLR,
  input  [3:0] ALUFlags,
  output PCSrc,
  output RegWrite,
  output MemWrite,
  output Mov_2,
  output BX_2
);

  wire and_1_out, and_2_out, and_3_out, Condition_Check_condex;
  wire [1:0] register_1_q, register_2_q;

  Register #(.width(2)) register_1 (.D(ALUFlags[3:2]), .en(and_2_out), .Q(register_1_q), .clk(CLK), .clr(CLR));
  Register #(.width(2)) register_2 (.D(ALUFlags[1:0]), .en(and_1_out), .Q(register_2_q), .clk(CLK), .clr(CLR));
  and and_1 (and_1_out, FlagW[0], Condition_Check_condex);
  and and_2 (and_2_out, FlagW[1], Condition_Check_condex);
  Condition_Check Condition_Check (
    .Cond(Cond), .Flags_3_2(register_1_q), .Flags_1_0(register_2_q), .CondEx(Condition_Check_condex));
  and and_3 (and_3_out, PCS, Condition_Check_condex);
  and and_4 (RegWrite, RegW, ~NoWrite, Condition_Check_condex);  // AND_Gate
  and and_5 (MemWrite, MemW, Condition_Check_condex);
  and and_6 (Mov_2, Mov, Condition_Check_condex);
  and and_7 (BX_2, BX, Condition_Check_condex);
  or or_1 (PCSrc, and_3_out, BX_2);
endmodule

module Condition_Check (
  input  [1:0] Flags_3_2,
  input  [1:0] Flags_1_0,
  input  [3:0] Cond,
  output CondEx
);

  wire and_1_out, not_1_out, not_2_out, xor_1_out, xor_2_out;

  xor xor_1 (xor_1_out, Flags_3_2[1], Flags_1_0[0]);
  xor xor_2 (xor_2_out, Flags_3_2[1], Flags_1_0[1]);
  not not_1 (not_1_out, xor_1_out);
  and and_1 (and_1_out, Flags_3_2[0], not_1_out);
  not not_2 (not_2_out, Flags_3_2[0]);
  Multiplexer #(.select(4)) multiplexer_1 (
    .in0(Flags_3_2[0]), .in1(not_2_out), .in11(xor_2_out), .in12(and_1_out), .in14(1'b1), .out(CondEx),
    .sel(Cond));  // open: in2, in3, in4, in5, in6, in7, in8, in9, in10, in13, in15, en
endmodule

module Extender (
  input  [1:0] ImmSrc,
  input  [23:0] _0_23,
  output [31:0] ExtImm
);

  wire [23:0] shifter_1_out;
  wire [31:0] bit_extender_1_out, bit_extender_2_out, bit_extender_3_out;

  Shifter #(.width(24)) shifter_1 (.in(_0_23), .\dist (5'b00010), .out(shifter_1_out));
  assign bit_extender_1_out = {{24{_0_23[7]}}, _0_23[7:0]};  // Bit_Extender bit_extender_1
  assign bit_extender_2_out = {{20{_0_23[11]}}, _0_23[11:0]};  // Bit_Extender bit_extender_2
  assign bit_extender_3_out = {{8{shifter_1_out[23]}}, shifter_1_out};  // Bit_Extender bit_extender_3
  Multiplexer #(.select(2), .width(32)) multiplexer_1 (
    .in0(bit_extender_1_out), .in1(bit_extender_2_out), .in2(bit_extender_3_out), .out(ExtImm), .sel(ImmSrc));  // open: in3, en
endmodule

module Logisim_LED (
  input  [31:0] in_1,
  output out_2
);

  // Probe on in_1
  Comparator #(.width(32)) comparator_1 (.a(in_1), .b(32'heafffffe), .eq(out_2));  // open: gt, lt
  LED led_1 (.in(out_2));
endmodule
